# Fritzing sketch Diagram Sketch (saved by Fritzing 1.0.6)
breadboards: 2

parts:
  M1 = DOIT Esp32 DevKit v1 (30 pins long, 11 pins width) [part_number=ESP32S-PIN30]
  DHT1 = DHT22 Humidity and Temperature Sensor
  DS1 = DS18B20 1-Wire Temperature Sensor Probe Cable
  S1 = LDR light sensor [package=THT]
  FC-1 = Sound Sensor
  SparkFun_Load_Cell_Amplifier_-_HX1 = SparkFun Load Cell Amplifier - HX711 [part_number=SEN-13879]

nets:
  VDD: M1.3V3, DHT1.VDD, DS1.VDD, S1.pin3, FC-1.VCC, SparkFun_Load_Cell_Amplifier_-_HX1.VDD
  GND: M1.GND, DHT1.GND, DS1.GND, S1.pin2, FC-1.GND, SparkFun_Load_Cell_Amplifier_-_HX1.GND
  N1: M1.D15, DHT1.DATA
  N2: M1.D4, DS1.DQ
  N3: M1.D21, SparkFun_Load_Cell_Amplifier_-_HX1.DAT
  N4: M1.D22, SparkFun_Load_Cell_Amplifier_-_HX1.SCK
  N5: M1.D34, S1.pin1
  N6: M1.D35, FC-1.OUT

custom parts:
  DOIT Esp32 DevKit v1 (30 pins long, 11 pins width): The DOIT Esp32 DevKit v1 is one of the development board created by DOIT to evaluate the ESP-WROOM-32 module. It is based on the ESP32 microcontroller that boasts Wifi, Bluetooth, Ethernet and Low Power support all in a single chip. (vanepp) made breadboard work, adjusted pin numbering and labels and reduced size of schematic and cleaned up pcb. This chip is 30pins long (2 x15) and 11 pins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
  LDR light sensor: Light sensor module. 3.3 V to 5V power.
  SparkFun Load Cell Amplifier - HX711: The SparkFun Load Cell Amplifier is a small breakout board for the HX711 IC that allows you to easily read load cells to measure weight. By connecting the amplifier to your microcontroller you will be able to read the changes in the resistance of the load cell, and with some calibration you’ll be able to get very accurate weight measurements. This can be handy for creating your own industrial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
